// Logisim project 16-bit-CPU.circ as structural Verilog
module _16_bit_ALU (
  input  [15:0] A,
  input  [15:0] B,
  input  [1:0] ALU_Op,
  output [15:0] ALU_Out
);

  wire and_1_out;
  wire [15:0] adder_1_out, and_2_out, multiplexer_1_out, not_1_out, or_1_out;

  Multiplexer #(.width(16), .enable("false")) multiplexer_1 (
    .in0(B), .in1(not_1_out), .out(multiplexer_1_out), .sel(and_1_out));
  assign not_1_out = ~B;  // NOT_Gate not_1, 16 bits wide
  and and_1 (and_1_out, ALU_Op[0], ALU_Op[1]);
  Adder #(.width(16)) adder_1 (.a(A), .b(multiplexer_1_out), .out(adder_1_out), .cin(and_1_out));  // open: cout
  assign and_2_out = multiplexer_1_out & A;  // AND_Gate and_2, 16 bits wide
  assign or_1_out = multiplexer_1_out | A;  // OR_Gate or_1, 16 bits wide
  Multiplexer #(.select(2), .width(16), .enable("false")) multiplexer_2 (
    .in0(adder_1_out), .in1(and_2_out), .in2(or_1_out), .in3(adder_1_out), .out(ALU_Out), .sel(ALU_Op));
endmodule

module _8x16_bit_Register_File (
  input  [15:0] Data_In,
  input  [2:0] Read_Addr_1,
  input  Write_Enable,
  input  [2:0] Write_Addr,
  input  [2:0] Read_Addr_2,
  input  Clock,
  output [15:0] Read_1_Data,
  output [15:0] Read_2_Data
);

  wire demultiplexer_1_out0, demultiplexer_1_out1, demultiplexer_1_out2, demultiplexer_1_out3,
       demultiplexer_1_out4, demultiplexer_1_out5, demultiplexer_1_out6, demultiplexer_1_out7;
  wire [15:0] register_1_q, register_2_q, register_3_q, register_4_q, register_5_q, register_6_q,
       register_7_q, register_8_q;

  Demultiplexer #(.select(3), .enable("false")) demultiplexer_1 (
    .out0(demultiplexer_1_out0), .out1(demultiplexer_1_out1), .out2(demultiplexer_1_out2),
    .out3(demultiplexer_1_out3), .out4(demultiplexer_1_out4), .out5(demultiplexer_1_out5),
    .out6(demultiplexer_1_out6), .out7(demultiplexer_1_out7), .in(Write_Enable), .sel(Write_Addr));
  Register #(.width(16)) register_1 (
    .D(Data_In), .en(demultiplexer_1_out0), .Q(register_1_q), .clk(Clock));  // open: clr
  Register #(.width(16)) register_2 (
    .D(Data_In), .en(demultiplexer_1_out1), .Q(register_2_q), .clk(Clock));  // open: clr
  Register #(.width(16)) register_3 (
    .D(Data_In), .en(demultiplexer_1_out2), .Q(register_3_q), .clk(Clock));  // open: clr
  Register #(.width(16)) register_4 (
    .D(Data_In), .en(demultiplexer_1_out3), .Q(register_4_q), .clk(Clock));  // open: clr
  Register #(.width(16)) register_5 (
    .D(Data_In), .en(demultiplexer_1_out4), .Q(register_5_q), .clk(Clock));  // open: clr
  Register #(.width(16)) register_6 (
    .D(Data_In), .en(demultiplexer_1_out5), .Q(register_6_q), .clk(Clock));  // open: clr
  Register #(.width(16)) register_7 (
    .D(Data_In), .en(demultiplexer_1_out6), .Q(register_7_q), .clk(Clock));  // open: clr
  Register #(.width(16)) register_8 (
    .D(Data_In), .en(demultiplexer_1_out7), .Q(register_8_q), .clk(Clock));  // open: clr
  Multiplexer #(.select(3), .width(16), .enable("false")) multiplexer_1 (
    .in0(register_1_q), .in1(register_2_q), .in2(register_3_q), .in3(register_4_q), .in4(register_5_q),
    .in5(register_6_q), .in6(register_7_q), .in7(register_8_q), .out(Read_1_Data), .sel(Read_Addr_1));
  Multiplexer #(.select(3), .width(16), .enable("false")) multiplexer_2 (
    .in0(register_1_q), .in1(register_2_q), .in2(register_3_q), .in3(register_4_q), .in4(register_5_q),
    .in5(register_6_q), .in6(register_7_q), .in7(register_8_q), .out(Read_2_Data), .sel(Read_Addr_2));
endmodule

module _16_bit_CPU (
  input  Clock
);

  wire adder_1_cout, control_logic_1_imm, control_logic_1_lw, control_logic_1_sw, not_1_out;
  wire [1:0] control_logic_1_op;
  wire [2:0] multiplexer_1_out;
  wire [4:0] adder_1_out, Program_Counter_q;
  wire [13:0] ram_1_data;
  wire [15:0] bit_extender_1_out, multiplexer_2_out, multiplexer_3_out,
       n8x16_bit_register_file_1_read_1_data, n8x16_bit_register_file_1_read_2_data, n16_bit_alu_1_alu_out,
       ram_2_data;

  Adder #(.width(5)) adder_1 (
    .a(Program_Counter_q), .b(5'b00001), .out(adder_1_out), .cin(adder_1_cout), .cout(adder_1_cout));
  Register #(.width(5)) Program_Counter (.D(adder_1_out), .Q(Program_Counter_q), .clk(Clock));  // open: en, clr
  RAM #(.addrWidth(5), .dataWidth(14)) ram_1 (
    .addr(Program_Counter_q), .data(ram_1_data), .sel(1'b1), .clk(Clock));  // open: ld, clr
  not not_1 (not_1_out, control_logic_1_sw);
  Control_Logic control_logic_1 (
    .OPCODE(ram_1_data[13:9]), .Imm(control_logic_1_imm), .SW(control_logic_1_sw), .LW(control_logic_1_lw),
    .OP(control_logic_1_op));
  _8x16_bit_Register_File u_8x16_bit_register_file_1 (
    .Data_In(multiplexer_3_out), .Write_Enable(not_1_out), .Clock(Clock), .Write_Addr(ram_1_data[8:6]),
    .Read_Addr_1(ram_1_data[5:3]), .Read_Addr_2(multiplexer_1_out),
    .Read_1_Data(n8x16_bit_register_file_1_read_1_data), .Read_2_Data(n8x16_bit_register_file_1_read_2_data));
  Multiplexer #(.width(3), .enable("false")) multiplexer_1 (
    .in0(ram_1_data[2:0]), .in1(ram_1_data[8:6]), .out(multiplexer_1_out), .sel(control_logic_1_sw));
  assign bit_extender_1_out = {{13{ram_1_data[2]}}, ram_1_data[2:0]};  // Bit_Extender bit_extender_1
  Multiplexer #(.width(16), .enable("false")) multiplexer_2 (
    .in0(n8x16_bit_register_file_1_read_2_data), .in1(bit_extender_1_out), .out(multiplexer_2_out),
    .sel(control_logic_1_imm));
  Multiplexer #(.width(16), .enable("false")) multiplexer_3 (
    .in0(n16_bit_alu_1_alu_out), .in1(ram_2_data), .out(multiplexer_3_out), .sel(control_logic_1_lw));
  _16_bit_ALU u_16_bit_alu_1 (
    .A(n8x16_bit_register_file_1_read_1_data), .B(multiplexer_2_out), .ALU_Op(control_logic_1_op),
    .ALU_Out(n16_bit_alu_1_alu_out));
  RAM #(.addrWidth(16), .dataWidth(16), .bus("separate")) ram_2 (
    .addr(n16_bit_alu_1_alu_out), .din(n8x16_bit_register_file_1_read_2_data), .data(ram_2_data),
    .str(control_logic_1_sw), .sel(1'b1), .clk(Clock), .ld(control_logic_1_lw));  // open: clr
endmodule

module Control_Logic (
  input  [4:0] OPCODE,
  output Imm,
  output SW,
  output LW,
  output [1:0] OP
);


  assign Imm = OPCODE[4];
  assign LW = OPCODE[2];
  assign OP = OPCODE[1:0];
  assign SW = OPCODE[3];
endmodule
