// Logisim project 16-bit-CPU.circ as structural Verilog
module _16_bit_ALU (
  input  [15:0] A,
  input  [15:0] B,
  input  [1:0] ALU_Op,
  output [15:0] ALU_Out,
  output Zero_Flag
);

  wire and_1_out;
  wire [15:0] and_2_out, multiplexer_1_out, n16_bit_cla_1_s, not_1_out, or_1_out;

  Multiplexer #(.width(16), .enable("false")) multiplexer_1 (
    .in0(B), .in1(not_1_out), .out(multiplexer_1_out), .sel(and_1_out));
  assign not_1_out = ~B;  // NOT_Gate not_1, 16 bits wide
  and and_1 (and_1_out, ALU_Op[0], ALU_Op[1]);
  _16_bit_CLA u_16_bit_cla_1 (.A(A), .B(multiplexer_1_out), .Cin(and_1_out), .S(n16_bit_cla_1_s));  // open: Cout
  assign and_2_out = multiplexer_1_out & A;  // AND_Gate and_2, 16 bits wide
  assign or_1_out = multiplexer_1_out | A;  // OR_Gate or_1, 16 bits wide
  Multiplexer #(.select(2), .width(16), .enable("false")) multiplexer_2 (
    .in0(n16_bit_cla_1_s), .in1(and_2_out), .in2(or_1_out), .in3(n16_bit_cla_1_s), .out(ALU_Out), .sel(ALU_Op));
  Comparator #(.width(16)) comparator_1 (.a(ALU_Out), .b({16{1'b0}}), .eq(Zero_Flag));  // open: gt, lt
endmodule

module _8x16_bit_Register_File (
  input  [15:0] Data_In,
  input  [2:0] Read_Addr_1,
  input  Write_Enable,
  input  [2:0] Write_Addr,
  input  [2:0] Read_Addr_2,
  input  Clock,
  output [15:0] Read_1_Data,
  output [15:0] Read_2_Data
);

  wire demultiplexer_1_out0, demultiplexer_1_out1, demultiplexer_1_out2, demultiplexer_1_out3,
       demultiplexer_1_out4, demultiplexer_1_out5, demultiplexer_1_out6, demultiplexer_1_out7;
  wire [15:0] register_1_q, register_2_q, register_3_q, register_4_q, register_5_q, register_6_q,
       register_7_q, register_8_q;

  Demultiplexer #(.select(3), .enable("false")) demultiplexer_1 (
    .out0(demultiplexer_1_out0), .out1(demultiplexer_1_out1), .out2(demultiplexer_1_out2),
    .out3(demultiplexer_1_out3), .out4(demultiplexer_1_out4), .out5(demultiplexer_1_out5),
    .out6(demultiplexer_1_out6), .out7(demultiplexer_1_out7), .in(Write_Enable), .sel(Write_Addr));
  Register #(.width(16)) register_1 (
    .D(Data_In), .en(demultiplexer_1_out0), .Q(register_1_q), .clk(Clock));  // open: clr
  Register #(.width(16)) register_2 (
    .D(Data_In), .en(demultiplexer_1_out1), .Q(register_2_q), .clk(Clock));  // open: clr
  Register #(.width(16)) register_3 (
    .D(Data_In), .en(demultiplexer_1_out2), .Q(register_3_q), .clk(Clock));  // open: clr
  Register #(.width(16)) register_4 (
    .D(Data_In), .en(demultiplexer_1_out3), .Q(register_4_q), .clk(Clock));  // open: clr
  Register #(.width(16)) register_5 (
    .D(Data_In), .en(demultiplexer_1_out4), .Q(register_5_q), .clk(Clock));  // open: clr
  Register #(.width(16)) register_6 (
    .D(Data_In), .en(demultiplexer_1_out5), .Q(register_6_q), .clk(Clock));  // open: clr
  Register #(.width(16)) register_7 (
    .D(Data_In), .en(demultiplexer_1_out6), .Q(register_7_q), .clk(Clock));  // open: clr
  Register #(.width(16)) register_8 (
    .D(Data_In), .en(demultiplexer_1_out7), .Q(register_8_q), .clk(Clock));  // open: clr
  Multiplexer #(.select(3), .width(16), .enable("false")) multiplexer_1 (
    .in0(register_1_q), .in1(register_2_q), .in2(register_3_q), .in3(register_4_q), .in4(register_5_q),
    .in5(register_6_q), .in6(register_7_q), .in7(register_8_q), .out(Read_1_Data), .sel(Read_Addr_1));
  Multiplexer #(.select(3), .width(16), .enable("false")) multiplexer_2 (
    .in0(register_1_q), .in1(register_2_q), .in2(register_3_q), .in3(register_4_q), .in4(register_5_q),
    .in5(register_6_q), .in6(register_7_q), .in7(register_8_q), .out(Read_2_Data), .sel(Read_Addr_2));
endmodule

module _16_bit_CPU (
  input  Clock,
  output [15:0] out_2,
  output [8:0] out_3,
  output [15:0] out_4,
  output [15:0] out_5,
  output [6:0] out_6
);

  wire and_1_out, control_logic_1_beq, control_logic_1_imm, control_logic_1_jump, control_logic_1_lw,
       control_logic_1_sw, n16_bit_alu_1_zero_flag, not_1_out, or_1_out;
  wire [1:0] control_logic_1_op;
  wire [2:0] multiplexer_3_out;
  wire [15:0] adder_1_out, bit_extender_2_out, bit_extender_3_out, multiplexer_1_out, multiplexer_2_out,
       multiplexer_4_out, multiplexer_5_out, n8x16_bit_register_file_1_read_1_data,
       n8x16_bit_register_file_1_read_2_data, n16_bit_alu_1_alu_out, n16_bit_alu_2_alu_out, ram_2_data;

  assign out_4 = {{7{1'b0}}, out_3};  // Bit_Extender bit_extender_1
  Adder #(.width(16)) adder_1 (.a(out_2), .b(16'h1), .out(adder_1_out));  // open: cin, cout
  Multiplexer #(.width(16), .enable("false")) multiplexer_1 (
    .in0(adder_1_out), .in1(n16_bit_alu_2_alu_out), .out(multiplexer_1_out), .sel(and_1_out));
  Multiplexer #(.width(16), .enable("false")) multiplexer_2 (
    .in0(multiplexer_1_out), .in1(out_4), .out(multiplexer_2_out), .sel(control_logic_1_jump));
  Register #(.width(16)) Program_Counter (.D(multiplexer_2_out), .Q(out_2), .clk(Clock));  // open: en, clr
  RAM #(.addrWidth(16), .dataWidth(16)) ram_1 (
    .addr(out_2), .data({out_5[15:9], out_3}), .sel(1'b1), .clk(Clock));  // open: ld, clr
  not not_1 (not_1_out, or_1_out);
  or or_1 (or_1_out, control_logic_1_beq, control_logic_1_sw);
  Control_Logic control_logic_1 (
    .OPCODE(out_5[15:9]), .Imm(control_logic_1_imm), .SW(control_logic_1_sw), .LW(control_logic_1_lw),
    .OP(control_logic_1_op), .Jump(control_logic_1_jump), .BEQ(control_logic_1_beq));
  _8x16_bit_Register_File u_8x16_bit_register_file_1 (
    .Data_In(multiplexer_5_out), .Write_Enable(not_1_out), .Clock(Clock), .Write_Addr(out_3[8:6]),
    .Read_Addr_1(out_3[5:3]), .Read_Addr_2(multiplexer_3_out),
    .Read_1_Data(n8x16_bit_register_file_1_read_1_data), .Read_2_Data(n8x16_bit_register_file_1_read_2_data));
  Multiplexer #(.width(3), .enable("false")) multiplexer_3 (
    .in0(out_3[2:0]), .in1(out_3[8:6]), .out(multiplexer_3_out), .sel(control_logic_1_sw));
  assign bit_extender_2_out = {{13{out_3[2]}}, out_3[2:0]};  // Bit_Extender bit_extender_2
  Multiplexer #(.width(16), .enable("false")) multiplexer_4 (
    .in0(n8x16_bit_register_file_1_read_2_data), .in1(bit_extender_2_out), .out(multiplexer_4_out),
    .sel(control_logic_1_imm));
  assign bit_extender_3_out = {{13{1'b0}}, out_3[8:6]};  // Bit_Extender bit_extender_3
  and and_1 (and_1_out, n16_bit_alu_1_zero_flag, control_logic_1_beq);
  Multiplexer #(.width(16), .enable("false")) multiplexer_5 (
    .in0(n16_bit_alu_1_alu_out), .in1(ram_2_data), .out(multiplexer_5_out), .sel(control_logic_1_lw));
  _16_bit_ALU u_16_bit_alu_1 (
    .A(n8x16_bit_register_file_1_read_1_data), .B(multiplexer_4_out), .ALU_Op(control_logic_1_op),
    .ALU_Out(n16_bit_alu_1_alu_out), .Zero_Flag(n16_bit_alu_1_zero_flag));
  _16_bit_ALU u_16_bit_alu_2 (
    .A(bit_extender_3_out), .B(adder_1_out), .ALU_Op(2'b00), .ALU_Out(n16_bit_alu_2_alu_out));  // open: Zero_Flag
  RAM #(.addrWidth(16), .dataWidth(16), .bus("separate")) ram_2 (
    .addr(n16_bit_alu_1_alu_out), .din(n8x16_bit_register_file_1_read_2_data), .data(ram_2_data),
    .str(control_logic_1_sw), .sel(1'b1), .clk(Clock), .ld(control_logic_1_lw));  // open: clr

  assign out_5[8:0] = out_3;
  assign out_6 = out_5[15:9];
endmodule

module Control_Logic (
  input  [6:0] OPCODE,
  output Imm,
  output SW,
  output LW,
  output [1:0] OP,
  output Jump,
  output BEQ
);


  assign BEQ = OPCODE[0];
  assign Imm = OPCODE[6];
  assign Jump = OPCODE[1];
  assign LW = OPCODE[4];
  assign OP = OPCODE[3:2];
  assign SW = OPCODE[5];
endmodule

module _4_bit_CLA_block (
  input  Cin,
  input  [3:0] A,
  input  [3:0] B,
  output [3:0] S,
  output Cout
);

  wire adder_1_cout, adder_2_cout, adder_3_cout;

  Adder #(.width(1)) adder_1 (.a(A[0]), .b(B[0]), .out(S[0]), .cin(Cin), .cout(adder_1_cout));
  Adder #(.width(1)) adder_2 (.a(A[1]), .b(B[1]), .out(S[1]), .cin(adder_1_cout), .cout(adder_2_cout));
  Adder #(.width(1)) adder_3 (.a(A[2]), .b(B[2]), .out(S[2]), .cin(adder_2_cout), .cout(adder_3_cout));
  Adder #(.width(1)) adder_4 (.a(A[3]), .b(B[3]), .out(S[3]), .cin(adder_3_cout), .cout(Cout));
endmodule

module _16_bit_CLA (
  input  Cin,
  input  [15:0] A,
  input  [15:0] B,
  output [15:0] S,
  output Cout
);

  wire n4_bit_cla_block_1_cout, n4_bit_cla_block_2_cout, n4_bit_cla_block_3_cout;

  _4_bit_CLA_block u_4_bit_cla_block_1 (.A(A[3:0]), .B(B[3:0]), .Cin(Cin), .Cout(n4_bit_cla_block_1_cout), .S(S[3:0]));
  _4_bit_CLA_block u_4_bit_cla_block_2 (
    .A(A[7:4]), .B(B[7:4]), .Cin(n4_bit_cla_block_1_cout), .Cout(n4_bit_cla_block_2_cout), .S(S[7:4]));
  _4_bit_CLA_block u_4_bit_cla_block_3 (
    .A(A[11:8]), .B(B[11:8]), .Cin(n4_bit_cla_block_2_cout), .Cout(n4_bit_cla_block_3_cout), .S(S[11:8]));
  _4_bit_CLA_block u_4_bit_cla_block_4 (
    .A(A[15:12]), .B(B[15:12]), .Cin(n4_bit_cla_block_3_cout), .Cout(Cout), .S(S[15:12]));
endmodule
